# Fritzing sketch GyverGun (saved by Fritzing 0.9.3b)
circuit board: 8.46667cm x 5.64444cm

parts:
  Часть1 = Arduino Nano (Rev3.0) (ICSP)
  L1 = Solenoid [part_number="Solenoid valve"]
  D2 = Diode [part_number=1N4007 package=diode-hv]
  R1 = Resistor [tolerance=±5% resistance=100 package="1206 [SMD]"]
  U4 = LIPO-1000mAh [part_number="12 VOLT" package=lipo-1000]
  R2 = Resistor [tolerance=±5% resistance=10k package="1206 [SMD]"]
  Q2 = Basic FET N-Channel [part_number=IRL3705N package="TO220 [THT]"]
  S2 = Round Pushbutton [part_number=Trigger]
  J1 = Basic Servo
  U2 = SWITCH_SPDT [part_number="Shooting mode" package=kps-1290]

nets:
  GND: Часть1.GND, U4.-, R2.Pin_1, Q2.source, S2.leg0, J1.gnd, U2.S
  N1: Часть1.D2, R1.Pin_1
  N2: Часть1.D3, S2.leg1
  N3: Часть1.D4, J1.pulse
  N4: Часть1.D5, U2.P
  N5: Часть1.VIN, L1.pin2, D2.C, U4.+
  5V: Часть1.5V, J1.vcc
  N6: L1.pin1, D2.A, Q2.drain
  N7: R1.Pin_0, R2.Pin_0, Q2.gate

notes:
  12V (3S) battery
