# Fritzing sketch TX (saved by Fritzing 0.9.3b)

parts:
  nRF24L01_PA1 = nRF24L01 power adapter [package="DIP (Dual Inline) [THT]"]
  Часть2 = Arduino Nano (Rev3.0)
  LED1 = smd LED [color="Red (633nm)" package="0603 [SMD]"]
  LED2 = smd LED [color="Green (555nm)" package="0603 [SMD]"]
  R1 = Resistor [tolerance=±5% resistance=220 package="2512 [SMD]"]
  R2 = Resistor [tolerance=±5% resistance=220 package="2512 [SMD]"]
  R3 = Slide Potentiometer
  S1 = Toggle Switch [package=THT]

nets:
  GND: nRF24L01_PA1.GND, Часть2.GND, LED1.cathode, LED2.cathode, R3.GND, S1.L2
  VCC: nRF24L01_PA1.VCC, Часть2.5V, R3.VCC
  N1: nRF24L01_PA1.CE, Часть2.D9
  N2: nRF24L01_PA1.CSN, Часть2.D10
  N3: nRF24L01_PA1.SCK, Часть2.D13/SCK
  N4: nRF24L01_PA1.MO, Часть2.D11/MOSI
  N5: nRF24L01_PA1.MI, Часть2.D12/MISO
  N6: Часть2.D4, S1.COM
  N7: Часть2.A2, R3.VRx
  N8: Часть2.A1, R3.VRy
  N9: Часть2.A0, R3.SW
  N10: LED1.anode, R2.Pin_1
  N11: LED2.anode, R1.Pin_1

notes:
  12V battery

custom parts:
  nRF24L01 power adapter: Адаптер для питания nRF
  Slide Potentiometer: A sliding adjustable resistor (potentiometer).
